// Logisim project canderson_lab3.circ as structural Verilog: 1 circuit, main circuit main
module main (
  input  A,
  input  B,
  output Q,
  output S
);

  wire INVERT_out;

  not INVERT (INVERT_out, A);
  xor XOR (Q, INVERT_out, B);
  and AND (S, Q, B);
endmodule
