// Logisim project lab4.circ as structural Verilog: 2 circuits, main circuit main
module main (
  input  Cin,
  input  [3:0] A,
  input  [3:0] B,
  output [3:0] Sum,
  output Cout
);

  wire n1_bit_full_adder_1_cout, n1_bit_full_adder_2_cout, n1_bit_full_adder_3_cout;

  _1_bit_Full_Adder u_1_bit_full_adder_1 (.A(A[0]), .B(B[0]), .Cin(Cin), .Sum(Sum[0]), .Cout(n1_bit_full_adder_1_cout));
  _1_bit_Full_Adder u_1_bit_full_adder_2 (
    .A(A[1]), .B(B[1]), .Cin(n1_bit_full_adder_1_cout), .Sum(Sum[1]), .Cout(n1_bit_full_adder_2_cout));
  _1_bit_Full_Adder u_1_bit_full_adder_3 (
    .A(A[2]), .B(B[2]), .Cin(n1_bit_full_adder_2_cout), .Sum(Sum[2]), .Cout(n1_bit_full_adder_3_cout));
  _1_bit_Full_Adder u_1_bit_full_adder_4 (
    .A(A[3]), .B(B[3]), .Cin(n1_bit_full_adder_3_cout), .Sum(Sum[3]), .Cout(Cout));

  // Notes on the sheet:
  //   4-bit Full Adder
endmodule

module _1_bit_Full_Adder (
  input  A,
  input  B,
  input  Cin,
  output Sum,
  output Cout
);

  wire and_1_out, and_2_out, xor_1_out;

  xor xor_1 (xor_1_out, B, Cin);
  and and_1 (and_1_out, B, Cin);
  xor xor_2 (Sum, A, xor_1_out);
  and and_2 (and_2_out, A, xor_1_out);
  or or_1 (Cout, and_2_out, and_1_out);

  // Notes on the sheet:
  //   1-bit Full Adder
endmodule
