// Logisim project lab6.circ as structural Verilog: 4 circuits, main circuit main
module main (
  input  [7:0] A,
  input  [7:0] B,
  input  Subtract,
  input  [1:0] OP,
  input  Write_Enable,
  output [7:0] Q,
  output Z,
  output N,
  output V
);

  wire and_1_out, and_2_out, nor_1_out, or_1_out;
  wire [7:0] and_3_out, n8_bit_full_adder_1_sum, not_1_out, or_2_out;

  and and_1 (and_1_out, ~B[7], ~A[7], Q[7]);  // AND_Gate
  and and_2 (and_2_out, B[7], A[7], ~Q[7]);  // AND_Gate
  or or_1 (or_1_out, and_1_out, and_2_out);
  assign not_1_out = ~A;  // NOT_Gate not_1, 8 bits wide
  assign and_3_out = A & B;  // AND_Gate and_3, 8 bits wide
  assign or_2_out = A | B;  // OR_Gate or_2, 8 bits wide
  _8_bit_Full_Adder u_8_bit_full_adder_1 (
    .A(A), .B(B), .Subtract(Subtract), .Sum(n8_bit_full_adder_1_sum));  // open: Cout
  Multiplexer #(.select(2), .width(8)) multiplexer_1 (
    .in0(not_1_out), .in1(and_3_out), .in2(or_2_out), .in3(n8_bit_full_adder_1_sum), .out(Q), .sel(OP));  // open: en
  nor nor_1 (nor_1_out, Q[0], Q[1], Q[2], Q[3], Q[4], Q[5], Q[6], Q[7]);
  D_Flip_Flop d_ff_1 (.D(nor_1_out), .WE(Write_Enable), .out_3(Z));  // open: out_4
  D_Flip_Flop d_ff_2 (.D(Q[7]), .WE(Write_Enable), .out_3(N));  // open: out_4
  D_Flip_Flop d_ff_3 (.D(or_1_out), .WE(Write_Enable), .out_3(V));  // open: out_4

  // Notes on the sheet:
  //   4-Function ALU
endmodule

module _1_bit_Full_Adder (
  input  A,
  input  B,
  input  Cin,
  output Sum,
  output Cout
);

  wire and_1_out, and_2_out, xor_1_out;

  xor xor_1 (xor_1_out, B, Cin);
  and and_1 (and_1_out, B, Cin);
  xor xor_2 (Sum, A, xor_1_out);
  and and_2 (and_2_out, A, xor_1_out);
  or or_1 (Cout, and_2_out, and_1_out);

  // Notes on the sheet:
  //   1-bit Full Adder
endmodule

module _8_bit_Full_Adder (
  input  [7:0] A,
  input  Subtract,
  input  [7:0] B,
  output [7:0] Sum,
  output Cout
);

  wire n1_bit_full_adder_1_cout, n1_bit_full_adder_2_cout, n1_bit_full_adder_3_cout,
       n1_bit_full_adder_4_cout, n1_bit_full_adder_5_cout, n1_bit_full_adder_6_cout,
       n1_bit_full_adder_7_cout, xor_1_out, xor_2_out, xor_3_out, xor_4_out, xor_5_out, xor_6_out, xor_7_out,
       xor_8_out;

  xor xor_1 (xor_1_out, B[0], Subtract);
  xor xor_2 (xor_2_out, B[1], Subtract);
  _1_bit_Full_Adder u_1_bit_full_adder_1 (
    .A(A[0]), .B(xor_1_out), .Cin(Subtract), .Sum(Sum[0]), .Cout(n1_bit_full_adder_1_cout));
  _1_bit_Full_Adder u_1_bit_full_adder_2 (
    .A(A[1]), .B(xor_2_out), .Cin(n1_bit_full_adder_1_cout), .Sum(Sum[1]), .Cout(n1_bit_full_adder_2_cout));
  _1_bit_Full_Adder u_1_bit_full_adder_3 (
    .A(A[2]), .B(xor_3_out), .Cin(n1_bit_full_adder_2_cout), .Sum(Sum[2]), .Cout(n1_bit_full_adder_3_cout));
  _1_bit_Full_Adder u_1_bit_full_adder_4 (
    .A(A[3]), .B(xor_4_out), .Cin(n1_bit_full_adder_3_cout), .Sum(Sum[3]), .Cout(n1_bit_full_adder_4_cout));
  _1_bit_Full_Adder u_1_bit_full_adder_5 (
    .A(A[4]), .B(xor_5_out), .Cin(n1_bit_full_adder_4_cout), .Sum(Sum[4]), .Cout(n1_bit_full_adder_5_cout));
  _1_bit_Full_Adder u_1_bit_full_adder_6 (
    .A(A[5]), .B(xor_6_out), .Cin(n1_bit_full_adder_5_cout), .Sum(Sum[5]), .Cout(n1_bit_full_adder_6_cout));
  _1_bit_Full_Adder u_1_bit_full_adder_7 (
    .A(A[6]), .B(xor_8_out), .Cin(n1_bit_full_adder_6_cout), .Sum(Sum[6]), .Cout(n1_bit_full_adder_7_cout));
  _1_bit_Full_Adder u_1_bit_full_adder_8 (
    .A(A[7]), .B(xor_7_out), .Cin(n1_bit_full_adder_7_cout), .Sum(Sum[7]), .Cout(Cout));
  xor xor_3 (xor_3_out, B[2], Subtract);
  xor xor_4 (xor_4_out, B[3], Subtract);
  xor xor_5 (xor_5_out, B[4], Subtract);
  xor xor_6 (xor_6_out, B[5], Subtract);
  xor xor_7 (xor_7_out, B[7], Subtract);
  xor xor_8 (xor_8_out, B[6], Subtract);

  // Notes on the sheet:
  //   8-bit Full Adder / Subtractor
endmodule

module D_Flip_Flop (
  input  D,
  input  WE,
  output out_3,
  output out_4
);

  wire nand_1_out, nand_2_out;

  nand nand_1 (nand_1_out, D, WE);
  nand nand_2 (nand_2_out, WE, ~D);  // NAND_Gate
  nand nand_3 (out_3, nand_1_out, out_4);
  nand nand_4 (out_4, out_3, nand_2_out);

  // Notes on the sheet:
  //   D Flip-Flop
endmodule
